// Logisim project sim.circ as structural Verilog: 3 circuits, main circuit main
module main (
);

  wire ALU_A_WE, ALU_B_WE, CLK;
  wire [15:0] A_q, B_q, C_q, D_q, E_q, IR_q, MAR_q, MDR_q, PC_q, ram_1_data;

  Clock clock_1 (.out(CLK));
  RAM #(.addrWidth(16), .dataWidth(16), .databus("bidir")) ram_1 (
    .addr(MAR_q), .we(1'b0), .oe(1'b0), .clk(CLK), .data(ram_1_data));
  Counter #(.max('hf), .width(4)) counter_1 ();  // open: clr, load, up, count, clk, D, carry, Q
  Register #(.width(16)) PC (.D(ram_1_data), .en(1'b0), .clk(CLK), .Q(PC_q));  // open: clr
  Register #(.width(16)) IR (.D(ram_1_data), .Q(IR_q));  // open: en, clk, clr
  assign ram_1_data = 1'b0 ? PC_q : 16'bz;  // Controlled_Buffer controlled_buffer_1
  Register #(.width(16)) MAR (.D(ram_1_data), .en(1'b0), .clk(CLK), .Q(MAR_q));  // open: clr
  Register #(.width(16)) MDR (.D(ram_1_data), .en(1'b0), .clk(CLK), .Q(MDR_q));  // open: clr
  assign ram_1_data = 1'b0 ? MDR_q : 16'bz;  // Controlled_Buffer controlled_buffer_2
  assign ram_1_data = 1'b0 ? IR_q : 16'bz;  // Controlled_Buffer controlled_buffer_3
  CTRL ctrl_1 (.I(IR_q));  // open: STEP, MDR_OE, PC_OE, IR_OE, MDR_WE, MAR_WE, PC_WE, A_WE, B_WE, C_WE, D_WE, E_WE, A_OE, B_OE, C_OE, D_OE, E_OE
  Register #(.width(16)) A (.D(ram_1_data), .en(1'b0), .clk(CLK), .Q(A_q));  // open: clr
  Register #(.width(16)) B (.D(ram_1_data), .en(1'b0), .clk(CLK), .Q(B_q));  // open: clr
  Register #(.width(16)) C (.D(ram_1_data), .en(1'b0), .clk(CLK), .Q(C_q));  // open: clr
  Register #(.width(16)) D (.D(ram_1_data), .en(1'b0), .clk(CLK), .Q(D_q));  // open: clr
  Register #(.width(16)) E (.D(ram_1_data), .en(1'b0), .clk(CLK), .Q(E_q));  // open: clr
  assign ram_1_data = 1'b0 ? A_q : 16'bz;  // Controlled_Buffer controlled_buffer_4
  assign ram_1_data = 1'b0 ? B_q : 16'bz;  // Controlled_Buffer controlled_buffer_5
  assign ram_1_data = 1'b0 ? C_q : 16'bz;  // Controlled_Buffer controlled_buffer_6
  assign ram_1_data = 1'b0 ? D_q : 16'bz;  // Controlled_Buffer controlled_buffer_7
  assign ram_1_data = 1'b0 ? E_q : 16'bz;  // Controlled_Buffer controlled_buffer_8
  ALU alu_1 (
    .A(ram_1_data), .A_WE(ALU_A_WE), .B(ram_1_data), .B_WE(ALU_B_WE), .CLK(CLK), .OP(IR_q[3:0]));  // open: S, C, Z, P
endmodule

module ALU (
  input  [15:0] A,
  input  A_WE,
  input  [15:0] B,
  input  B_WE,
  input  CLK,
  input  [3:0] OP,
  output [15:0] S,
  output C,
  output Z,
  output P
);

  wire and_2_out, not_1_out, not_2_out, not_3_out, or_2_out, xor_3_out, xor_4_out;
  wire [15:0] adder_1_out, and_1_out, bit_extender_1_out, multiplexer_1_out, multiplexer_2_out,
       multiplexer_3_out, multiplexer_4_out, or_1_out, register_1_q, register_2_q, shifter_1_out,
       shifter_2_out, xor_1_out, xor_2_out;

  Register #(.width(16)) register_1 (.D(A), .en(A_WE), .clk(CLK), .Q(register_1_q));  // open: clr
  Register #(.width(16)) register_2 (.D(B), .en(B_WE), .clk(CLK), .Q(register_2_q));  // open: clr
  not not_1 (not_1_out, OP[0]);
  assign bit_extender_1_out = {{15{not_1_out}}, not_1_out};  // Bit_Extender bit_extender_1
  assign xor_1_out = register_2_q ^ bit_extender_1_out;  // XOR_Gate xor_1, 16 bits wide
  assign or_1_out = register_1_q | register_2_q;  // OR_Gate or_1, 16 bits wide
  Multiplexer #(.width(16)) multiplexer_1 (.in0(or_1_out), .in1(and_1_out), .out(multiplexer_1_out), .sel(not_2_out));
  assign and_1_out = register_1_q & register_2_q;  // AND_Gate and_1, 16 bits wide
  not not_2 (not_2_out, OP[0]);
  assign xor_2_out = register_1_q ^ register_2_q;  // XOR_Gate xor_2, 16 bits wide
  Multiplexer #(.width(16)) multiplexer_2 (
    .in0(xor_2_out), .in1(shifter_1_out), .out(multiplexer_2_out), .sel(not_3_out));
  Shifter #(.width(16)) shifter_1 (.in(register_1_q), .\dist (register_2_q[3:0]), .out(shifter_1_out));
  not not_3 (not_3_out, OP[0]);
  Shifter #(.shift("lr"), .width(16)) shifter_2 (.in(register_1_q), .\dist (register_2_q[3:0]), .out(shifter_2_out));
  Adder #(.width(16)) adder_1 (.a(register_1_q), .b(xor_1_out), .out(adder_1_out), .cin(not_1_out), .cout(C));
  xor xor_3 (xor_3_out, OP[0], OP[1]);
  xor xor_4 (xor_4_out, OP[0], OP[1]);
  Multiplexer #(.width(16)) multiplexer_3 (
    .in0(adder_1_out), .in1(multiplexer_1_out), .out(multiplexer_3_out), .sel(xor_3_out));
  Multiplexer #(.width(16)) multiplexer_4 (
    .in0(multiplexer_2_out), .in1(shifter_2_out), .out(multiplexer_4_out), .sel(xor_4_out));
  Multiplexer #(.width(16)) multiplexer_5 (.in0(multiplexer_3_out), .in1(multiplexer_4_out), .out(S), .sel(or_2_out));
  or or_2 (or_2_out, and_2_out, OP[3]);
  and and_2 (and_2_out, OP[0], OP[1], OP[2]);

  // Notes on the sheet:
  //   0011: A+B
  //   0100: A-B
  //   0101: A v B
  //   0110: A ^ B
  //   0111: A xor B
  //   1000: A << B
  //   1001: A >> B
endmodule

module CTRL (
  input  [15:0] I,
  input  [3:0] STEP,
  output MDR_OE,
  output PC_OE,
  output IR_OE,
  output MDR_WE,
  output MAR_WE,
  output PC_WE,
  output A_WE,
  output B_WE,
  output C_WE,
  output D_WE,
  output E_WE,
  output A_OE,
  output B_OE,
  output C_OE,
  output D_OE,
  output E_OE
);
endmodule
